// Logisim project farm.circ as structural Verilog: 7 circuits, main circuit main
module main (
);

  wire clock, k2, k3, k4, k5, k6, kk2, kk3, kk4, kk5, kk6, \kůlna_1_koupit_pole_2 , or_1_out,
       pole_1_sklizeno, pole_2_sklizeno, pole_3_sklizeno, pole_4_sklizeno, pole_5_sklizeno, pole_6_sklizeno,
       prodej_pole_1_potvrzeni, Reset, Sklidit_2_out, Sklidit_3_out, Sklidit_4_out, Sklidit_5_out,
       Sklidit_6_out, Sklidit_out;
  wire [3:0] \dny_1__1_dnů , \dny_1__1_měsíců , \dny_1__10__dnů , \dny_1__10_měsíců , \kůlna_1__1_hodnota ,
       \kůlna_1__10_hodnota , \kůlna_1__100_hodnota ;
  wire [9:0] pole_1_pole_charge, pole_1_pole_done, pole_2_pole_charge, pole_2_pole_done, pole_3_pole_charge,
       pole_3_pole_done, pole_4_pole_charge, pole_4_pole_done, pole_5_pole_charge, pole_5_pole_done,
       pole_6_pole_charge, pole_6_pole_done;

  Button u_Reset (.out(Reset));
  Clock clock_1 (.out(clock));
  Dny dny_1 (
    .clock(clock), .reset(Reset), .\_10__dnů (\dny_1__10__dnů ), .\_1_dnů (\dny_1__1_dnů ),
    .\_10_měsíců (\dny_1__10_měsíců ), .\_1_měsíců (\dny_1__1_měsíců ));
  DotMatrix #(.matrixcols(1), .matrixrows(10)) dotmatrix_1 (.col0(pole_1_pole_charge));
  DotMatrix #(.matrixcols(10), .matrixrows(10)) dotmatrix_2 (
    .col0(pole_1_pole_done), .col1(pole_1_pole_done), .col2(pole_1_pole_done), .col3(pole_1_pole_done),
    .col4(pole_1_pole_done), .col5(pole_1_pole_done), .col6(pole_1_pole_done), .col7(pole_1_pole_done),
    .col8(pole_1_pole_done), .col9(pole_1_pole_done));
  Pole pole_1 (
    .clock(clock), .Reset(Reset), .sklidit_pole(Sklidit_out), .Zakoupit_pole(1'b1),
    .pole_charge(pole_1_pole_charge), .pole_done(pole_1_pole_done), .sklizeno(pole_1_sklizeno));
  DotMatrix #(.matrixcols(10), .matrixrows(10)) dotmatrix_3 (
    .col0(pole_2_pole_done), .col1(pole_2_pole_done), .col2(pole_2_pole_done), .col3(pole_2_pole_done),
    .col4(pole_2_pole_done), .col5(pole_2_pole_done), .col6(pole_2_pole_done), .col7(pole_2_pole_done),
    .col8(pole_2_pole_done), .col9(pole_2_pole_done));
  DotMatrix #(.matrixcols(1), .matrixrows(10)) dotmatrix_4 (.col0(pole_2_pole_charge));
  Pole pole_2 (
    .clock(clock), .Reset(Reset), .sklidit_pole(Sklidit_2_out), .Zakoupit_pole(kk4),
    .pole_charge(pole_2_pole_charge), .pole_done(pole_2_pole_done), .sklizeno(pole_2_sklizeno));
  Hex_Digit_Display hex_digit_display_1 (.value(\dny_1__1_dnů ));  // open: dp
  Hex_Digit_Display hex_digit_display_2 (.value(\dny_1__10__dnů ));  // open: dp
  Button Sklidit (.out(Sklidit_out));
  Button koupit (.out(k4));
  Button Sklidit_2 (.out(Sklidit_2_out));
  Hex_Digit_Display hex_digit_display_3 (.value(\dny_1__1_měsíců ));  // open: dp
  Hex_Digit_Display hex_digit_display_4 (.value(\dny_1__10_měsíců ));  // open: dp
  DotMatrix #(.matrixcols(1), .matrixrows(10)) dotmatrix_5 (.col0(pole_3_pole_charge));
  Pole pole_3 (
    .clock(clock), .Reset(Reset), .sklidit_pole(Sklidit_3_out), .Zakoupit_pole(kk2),
    .pole_charge(pole_3_pole_charge), .pole_done(pole_3_pole_done), .sklizeno(pole_3_sklizeno));
  DotMatrix #(.matrixcols(1), .matrixrows(10)) dotmatrix_6 (.col0(pole_4_pole_charge));
  Pole pole_4 (
    .clock(clock), .Reset(Reset), .sklidit_pole(Sklidit_4_out), .Zakoupit_pole(kk5),
    .pole_charge(pole_4_pole_charge), .pole_done(pole_4_pole_done), .sklizeno(pole_4_sklizeno));
  DotMatrix #(.matrixcols(10), .matrixrows(10)) dotmatrix_7 (
    .col0(pole_3_pole_done), .col1(pole_3_pole_done), .col2(pole_3_pole_done), .col3(pole_3_pole_done),
    .col4(pole_3_pole_done), .col5(pole_3_pole_done), .col6(pole_3_pole_done), .col7(pole_3_pole_done),
    .col8(pole_3_pole_done), .col9(pole_3_pole_done));
  Button koupit_2 (.out(k2));
  Button Sklidit_3 (.out(Sklidit_3_out));
  DotMatrix #(.matrixcols(10), .matrixrows(10)) dotmatrix_8 (
    .col0(pole_4_pole_done), .col1(pole_4_pole_done), .col2(pole_4_pole_done), .col3(pole_4_pole_done),
    .col4(pole_4_pole_done), .col5(pole_4_pole_done), .col6(pole_4_pole_done), .col7(pole_4_pole_done),
    .col8(pole_4_pole_done), .col9(pole_4_pole_done));
  Button koupit_3 (.out(k5));
  Button Sklidit_4 (.out(Sklidit_4_out));
  Pole pole_5 (
    .clock(clock), .Reset(Reset), .sklidit_pole(Sklidit_5_out), .Zakoupit_pole(kk3),
    .pole_charge(pole_5_pole_charge), .pole_done(pole_5_pole_done), .sklizeno(pole_5_sklizeno));
  Pole pole_6 (
    .clock(clock), .Reset(Reset), .sklidit_pole(Sklidit_6_out), .Zakoupit_pole(kk6),
    .pole_charge(pole_6_pole_charge), .pole_done(pole_6_pole_done), .sklizeno(pole_6_sklizeno));
  DotMatrix #(.matrixcols(10), .matrixrows(10)) dotmatrix_9 (
    .col0(pole_5_pole_done), .col1(pole_5_pole_done), .col2(pole_5_pole_done), .col3(pole_5_pole_done),
    .col4(pole_5_pole_done), .col5(pole_5_pole_done), .col6(pole_5_pole_done), .col7(pole_5_pole_done),
    .col8(pole_5_pole_done), .col9(pole_5_pole_done));
  DotMatrix #(.matrixcols(1), .matrixrows(10)) dotmatrix_10 (.col0(pole_5_pole_charge));
  Button koupit_4 (.out(k3));
  Button Sklidit_5 (.out(Sklidit_5_out));
  DotMatrix #(.matrixcols(1), .matrixrows(10)) dotmatrix_11 (.col0(pole_6_pole_charge));
  DotMatrix #(.matrixcols(10), .matrixrows(10)) dotmatrix_12 (
    .col0(pole_6_pole_done), .col1(pole_6_pole_done), .col2(pole_6_pole_done), .col3(pole_6_pole_done),
    .col4(pole_6_pole_done), .col5(pole_6_pole_done), .col6(pole_6_pole_done), .col7(pole_6_pole_done),
    .col8(pole_6_pole_done), .col9(pole_6_pole_done));
  Button koupit_5 (.out(k6));
  Button Sklidit_6 (.out(Sklidit_6_out));
  or or_1 (or_1_out, pole_1_sklizeno, pole_3_sklizeno, pole_5_sklizeno, pole_2_sklizeno, pole_4_sklizeno, pole_6_sklizeno);
  \Kůlna  \kůlna_1  (
    .sklidit(or_1_out), .reset(Reset), .Koupit_pole(prodej_pole_1_potvrzeni),
    ._1_hodnota(\kůlna_1__1_hodnota ), ._10_hodnota(\kůlna_1__10_hodnota ),
    ._100_hodnota(\kůlna_1__100_hodnota ), .koupit_pole_2(\kůlna_1_koupit_pole_2 ));
  Prodej_pole prodej_pole_1 (
    ._2(k2), ._3(k3), ._4(k4), ._5(k5), ._6(k6), .potvrzeno(\kůlna_1_koupit_pole_2 ),
    .potvrzeni(prodej_pole_1_potvrzeni), ._2_2(kk2), ._3_2(kk3), ._4_2(kk4), ._5_2(kk5), ._6_2(kk6));
  Hex_Digit_Display hex_digit_display_5 (.value(\kůlna_1__10_hodnota ));  // open: dp
  Hex_Digit_Display hex_digit_display_6 (.value(\kůlna_1__100_hodnota ));  // open: dp
  Hex_Digit_Display hex_digit_display_7 (.value(\kůlna_1__1_hodnota ));  // open: dp

  // Notes on the sheet:
  //   dny
  //   Měsíce
  //   Peníze
  //   milion Kč
endmodule

module Dny (
  input  clock,
  input  reset,
  output [3:0] \_10__dnů ,
  output [3:0] \_1_dnů ,
  output [3:0] \_10_měsíců ,
  output [3:0] \_1_měsíců 
);

  wire and_1_out, demultiplexer_1_out1, demultiplexer_1_out10, demultiplexer_2_out3, demultiplexer_3_out10,
       demultiplexer_4_out9, or_1_out, or_2_out, or_3_out, or_4_out;

  Counter #(.width(4), .max('hf)) counter_1 (
    .Q(\_10__dnů ), .clk(clock), .clr(or_1_out));  // open: load, D, count, carry
  or or_1 (or_1_out, reset, demultiplexer_1_out10);
  Demultiplexer #(.select(4)) demultiplexer_1 (
    .out1(demultiplexer_1_out1), .out10(demultiplexer_1_out10), .in(1'b1), .sel(\_10__dnů ));  // open: out0, out2, out3, out4, out5, out6, out7, out8, out9, out11, out12, out13, out14, out15, en
  or or_2 (or_2_out, reset, and_1_out);
  Counter #(.width(4), .max('hf)) counter_2 (
    .Q(\_1_dnů ), .clk(demultiplexer_1_out10), .clr(or_2_out));  // open: load, D, count, carry
  Demultiplexer #(.select(4)) demultiplexer_2 (
    .out3(demultiplexer_2_out3), .in(1'b1), .sel(\_1_dnů ));  // open: out0, out1, out2, out4, out5, out6, out7, out8, out9, out10, out11, out12, out13, out14, out15, en
  and and_1 (and_1_out, demultiplexer_1_out1, demultiplexer_2_out3);
  Demultiplexer #(.select(4)) demultiplexer_3 (
    .out10(demultiplexer_3_out10), .in(1'b1), .sel(\_10_měsíců ));  // open: out0, out1, out2, out3, out4, out5, out6, out7, out8, out9, out11, out12, out13, out14, out15, en
  Counter #(.width(4), .max('hf)) counter_3 (
    .Q(\_10_měsíců ), .clk(and_1_out), .clr(or_3_out));  // open: load, D, count, carry
  or or_3 (or_3_out, reset, demultiplexer_3_out10);
  Demultiplexer #(.select(4)) demultiplexer_4 (
    .out9(demultiplexer_4_out9), .in(1'b1), .sel(\_1_měsíců ));  // open: out0, out1, out2, out3, out4, out5, out6, out7, out8, out10, out11, out12, out13, out14, out15, en
  Counter #(.width(4), .max('hf)) counter_4 (
    .Q(\_1_měsíců ), .clk(demultiplexer_3_out10), .clr(or_4_out));  // open: load, D, count, carry
  or or_4 (or_4_out, reset, demultiplexer_4_out9);
endmodule

module Pole (
  input  clock,
  input  Reset,
  input  sklidit_pole,
  input  Zakoupit_pole,
  output [9:0] pole_charge,
  output [9:0] pole_done,
  output sklizeno
);

  wire and_1_out, and_3_out, demultiplexer_1_out3, demultiplexer_1_out6, demultiplexer_1_out9,
       demultiplexer_1_out12, demultiplexer_1_out15, demultiplexer_1_out18, demultiplexer_1_out21,
       demultiplexer_1_out24, demultiplexer_1_out27, demultiplexer_1_out30, or_1_out, sr_latch_1_output;
  wire [4:0] counter_1_q;

  SR_Latch sr_latch_1 (.reset(Reset), .set(Zakoupit_pole), .\output (sr_latch_1_output));
  Counter #(.width(5), .max('h1f)) counter_1 (
    .Q(counter_1_q), .clk(and_1_out), .clr(or_1_out));  // open: load, D, count, carry
  and and_1 (and_1_out, clock, sr_latch_1_output);
  Demultiplexer #(.select(5)) demultiplexer_1 (
    .out3(demultiplexer_1_out3), .out6(demultiplexer_1_out6), .out9(demultiplexer_1_out9),
    .out12(demultiplexer_1_out12), .out15(demultiplexer_1_out15), .out18(demultiplexer_1_out18),
    .out21(demultiplexer_1_out21), .out24(demultiplexer_1_out24), .out27(demultiplexer_1_out27),
    .out30(demultiplexer_1_out30), .in(1'b1), .sel(counter_1_q));  // open: out0, out1, out2, out4, out5, out7, out8, out10, out11, out13, out14, out16, out17, out19, out20, out22, out23, out25, out26, out28, out29, out31, en
  and and_2 (sklizeno, sklidit_pole, and_3_out);
  or or_1 (or_1_out, Reset, sklizeno);
  SR_Latch sr_latch_2 (.reset(or_1_out), .set(demultiplexer_1_out3), .\output (pole_charge[0]));
  SR_Latch sr_latch_3 (.reset(or_1_out), .set(demultiplexer_1_out6), .\output (pole_charge[1]));
  SR_Latch sr_latch_4 (.reset(or_1_out), .set(demultiplexer_1_out9), .\output (pole_charge[2]));
  SR_Latch sr_latch_5 (.reset(or_1_out), .set(demultiplexer_1_out12), .\output (pole_charge[3]));
  SR_Latch sr_latch_6 (.reset(or_1_out), .set(demultiplexer_1_out15), .\output (pole_charge[4]));
  SR_Latch sr_latch_7 (.reset(or_1_out), .set(demultiplexer_1_out18), .\output (pole_charge[5]));
  SR_Latch sr_latch_8 (.reset(or_1_out), .set(demultiplexer_1_out21), .\output (pole_charge[6]));
  SR_Latch sr_latch_9 (.reset(or_1_out), .set(demultiplexer_1_out24), .\output (pole_charge[7]));
  SR_Latch sr_latch_10 (.reset(or_1_out), .set(demultiplexer_1_out27), .\output (pole_charge[8]));
  SR_Latch sr_latch_11 (.reset(or_1_out), .set(demultiplexer_1_out30), .\output (pole_charge[9]));
  and and_3 (and_3_out, pole_charge[0], pole_charge[1], pole_charge[2], pole_charge[3], pole_charge[4], pole_charge[5], pole_charge[6], pole_charge[7], pole_charge[8], pole_charge[9]);
  assign pole_done = and_3_out ? {10{1'b1}} : 10'bz;  // Controlled_Buffer controlled_buffer_1
endmodule

// SR-L
module SR_Latch (
  input  reset,
  input  set,
  output \output 
);

  wire nor_2_out;

  nor nor_1 (\output , reset, nor_2_out);
  nor nor_2 (nor_2_out, \output , set);
endmodule

module \Kůlna  (
  input  sklidit,
  input  reset,
  input  Koupit_pole,
  output [3:0] _1_hodnota,
  output [3:0] _10_hodnota,
  output [3:0] _100_hodnota,
  output koupit_pole_2
);

  wire counter_1_carry, demultiplexer_1_out1, demultiplexer_1_out2, demultiplexer_1_out3,
       demultiplexer_1_out4, demultiplexer_1_out5, demultiplexer_1_out6, demultiplexer_1_out7,
       demultiplexer_1_out8, demultiplexer_1_out9, \max_hodnota_výstup , or_1_out, or_2_out, or_3_out,
       or_4_out;

  Counter #(.width(4), .max('ha)) counter_1 (
    .Q(_1_hodnota), .carry(counter_1_carry), .clk(sklidit), .clr(or_1_out));  // open: load, D, count
  or or_1 (or_1_out, reset, counter_1_carry);
  and and_1 (koupit_pole_2, Koupit_pole, or_4_out);
  or or_2 (or_2_out, koupit_pole_2, counter_1_carry);
  or or_3 (or_3_out, reset, \max_hodnota_výstup );
  Counter #(.width(4), .max('ha)) counter_2 (
    .load(koupit_pole_2), .Q(_10_hodnota), .clk(or_2_out), .clr(or_3_out));  // open: D, count, carry
  Demultiplexer #(.select(4)) demultiplexer_1 (
    .out1(demultiplexer_1_out1), .out2(demultiplexer_1_out2), .out3(demultiplexer_1_out3),
    .out4(demultiplexer_1_out4), .out5(demultiplexer_1_out5), .out6(demultiplexer_1_out6),
    .out7(demultiplexer_1_out7), .out8(demultiplexer_1_out8), .out9(demultiplexer_1_out9), .in(1'b1),
    .sel(_10_hodnota));  // open: out0, out10, out11, out12, out13, out14, out15, en
  max_hodnota max_hodnota (.vstup(_10_hodnota), .\výstup (\max_hodnota_výstup ));
  Counter #(.width(4), .max('h9)) counter_3 (
    .Q(_100_hodnota), .clk(\max_hodnota_výstup ), .clr(reset));  // open: load, D, count, carry
  or or_4 (or_4_out, demultiplexer_1_out1, demultiplexer_1_out2, demultiplexer_1_out3, demultiplexer_1_out4, demultiplexer_1_out5, demultiplexer_1_out6, demultiplexer_1_out7, demultiplexer_1_out8, demultiplexer_1_out9);

  // Other names for the same wires on the sheet: ZP = koupit_pole_2
endmodule

module max_hodnota (
  input  [3:0] vstup,
  output \výstup 
);

  Demultiplexer #(.select(4)) demultiplexer_1 (
    .out10(\výstup ), .in(1'b1), .sel(vstup));  // open: out0, out1, out2, out3, out4, out5, out6, out7, out8, out9, out11, out12, out13, out14, out15, en
endmodule

module Prodej_pole (
  input  _2,
  input  _3,
  input  _4,
  input  _5,
  input  _6,
  input  potvrzeno,
  output potvrzeni,
  output _2_2,
  output _3_2,
  output _4_2,
  output _5_2,
  output _6_2
);

  or or_1 (potvrzeni, _2, _3, _4, _5, _6);
  and and_1 (_2_2, _2, potvrzeno);
  and and_2 (_3_2, _3, potvrzeno);
  and and_3 (_4_2, _4, potvrzeno);
  and and_4 (_5_2, _5, potvrzeno);
  and and_5 (_6_2, _6, potvrzeno);
endmodule
